# Fritzing sketch PiezoStepperUno12V (saved by Fritzing 0.9.2b)

parts:
  Part1 = Arduino Uno (Rev3) - ICSP
  M2 = Stepper Motor - Bipolar
  Part2 = EasyDriver_v44
  J1 = Piezo Speaker
  12V = Power plug
  R1 = Resistor [tolerance=±5% resistance=1M package="2010 [SMD]"]

nets:
  N1: Part1.A0, J1.pin2, R1.Pin_0
  5V: Part1.5V, Part2.VCC
  N2: Part1.D2, Part2.STEP
  N3: Part1.D3_PWM, Part2.DIR
  N4: Part1.D4, Part2.MS1
  N5: Part1.D5_PWM, Part2.MS2
  N6: Part1.D6_PWM, Part2.ENABLE
  GND: Part1.GND, Part2.GND, J1.pin1, 12V.GND, R1.Pin_1
  VIN: Part1.VIN, Part2.V+, 12V.VCC
  N7: M2.A, Part2.OUT2A
  N8: M2.C, Part2.OUT2B
  N9: M2.B, Part2.OUT1A
  N10: M2.D, Part2.OUT1B
